# Fritzing sketch launcher_prototype_module_th_fet_5x5 (saved by Fritzing 0.7.4b)
breadboards: 1

parts:
  D1 = Rectifier Diode [part_number=1N4001 package="300 mil [THT]"]
  D2 = Rectifier Diode [part_number=1N4001 package="300 mil [THT]"]
  U1 = LM 358 Dual Op-Amp [package="DIP8 [THT]"]
  J1 = female pin header, 8 pins [form="♀ (female)"]
  R1 = Resistor [tolerance=±5% resistance=10k package=THT]
  R3 = Resistor [tolerance=±5% resistance=1k package=THT]
  R5 = Resistor [tolerance=±5% resistance=1k package=THT]
  R6 = Resistor [tolerance=±5% resistance=220k package=THT]
  R4 = Resistor [tolerance=±5% resistance=220k package=THT]
  D3 = Rectifier Diode [part_number=1N4001 package="300 mil [THT]"]
  D4 = Rectifier Diode [part_number=1N4001 package="300 mil [THT]"]
  R2 = Resistor [tolerance=±5% resistance=10k package=THT]
  C1 = Ceramic Capacitor [capacitance=100nF package="100 mil [THT, multilayer]"]
  R8 = Resistor [tolerance=±5% resistance=2.2k package=THT]
  R7 = Resistor [tolerance=±5% resistance=2.2k package=THT]
  Q2 = NPN-Transistor [part_number=BS170_D26Z package="TO92 [THT]"]
  Q1 = NPN-Transistor [package="TO92 [THT]"]
  C2 = Electrolytic Capacitor [capacitance=10µF voltage=16V package="100 mil [THT, electrolytic]"]
  J2 = screw terminal, 6 pins

nets:
  N1: D1.cathode, D2.cathode, J1.pin3, J2.pin1, J2.pin6
  N2: D1.anode, Q1.C, J2.pin2
  N3: D2.anode, Q2.C, J2.pin5
  N4: U1.connector0, J1.pin1, R4.Pin_1
  N5: U1.connector1, R3.Pin_0, R4.Pin_0, D4.cathode
  N6: U1.connector2, D4.anode, R7.Pin_1, J2.pin4
  GND: U1.connector3, J1.pin6, R1.Pin_0, R3.Pin_1, R5.Pin_1, R2.Pin_1, C1.1, Q2.E, Q1.E, C2.-
  N7: U1.connector4, D3.anode, R8.Pin_0, J2.pin3
  N8: U1.connector5, R5.Pin_0, R6.Pin_0, D3.cathode
  N9: U1.connector6, J1.pin8, R6.Pin_1
  N10: U1.connector7, J1.pin5, C1.0, R8.Pin_1, R7.Pin_0, C2.+
  N11: J1.pin2, R1.Pin_1, Q2.B
  N12: J1.pin7, R2.Pin_0, Q1.B

notes:
  Q1 and Q2 are actually FETs, Fritzing just didn't have a FET part with the right pinout, so went with what it has
